# Fritzing sketch setup (saved by Fritzing 0.8.0b)
breadboards: 1

parts:
  Part1 = Arduino Uno (Rev3)
  7_Segment1 = 7 Segment Display
  R1 = Resistor [tolerance=±5% resistance=220 package=THT]
  R2 = Resistor [tolerance=±5% resistance=220 package=THT]

nets:
  N1: Part1.D8, 7_Segment1.Segment_A
  N2: Part1.D9_PWM, 7_Segment1.Segment_B
  N3: Part1.D2, 7_Segment1.Segment_C
  N4: Part1.D3_PWM, 7_Segment1.Segment_D
  N5: Part1.D4, 7_Segment1.Segment_E
  N6: Part1.D5_PWM, 7_Segment1.Segment_G
  N7: Part1.D6_PWM, 7_Segment1.Segment_F
  N8: Part1.5V, R2.Pin_1
  N9: 7_Segment1.common_anode, R1.Pin_0, R2.Pin_0
