# Fritzing sketch AND_gate (saved by Fritzing 0.8.0b)
breadboards: 1

parts:
  Q1 = NPN-Transistor [package="TO92 [THT]"]
  Q2 = NPN-Transistor [package="TO92 [THT]"]
  R1 = Resistor [tolerance=±5% resistance=10k package=THT]
  R2 = Resistor [tolerance=±5% resistance=10k package=THT]
  LED1 = LED - 5mm [color="Red (633nm)" package="5 mm [THT]"]
  VCC1 = Battery

nets:
  N1: Q1.E, Q2.C
  N2: Q1.B, R1.Pin_0
  N3: Q1.C, VCC1.-
  N4: Q2.E, LED1.anode
  N5: Q2.B, R2.Pin_0
  GND: LED1.cathode
