# Fritzing sketch OR_gate (saved by Fritzing 0.8.0b)
breadboards: 1

parts:
  Q1 = NPN-Transistor [package="TO92 [THT]"]
  Q2 = NPN-Transistor [package="TO92 [THT]"]
  R1 = Resistor [tolerance=±5% resistance=10k package=THT]
  R2 = Resistor [tolerance=±5% resistance=10k package=THT]
  LED1 = LED - 5mm [color="Red (633nm)" package="5 mm [THT]"]
  VCC1 = Battery
  R3 = Resistor [tolerance=±5% resistance=4.7k package=THT]

nets:
  N1: Q1.E, Q2.E, LED1.anode, R3.Pin_0
  N2: Q1.B, R1.Pin_0
  N3: Q1.C, Q2.C, VCC1.-
  N4: Q2.B, R2.Pin_0
  GND: R3.Pin_1
